# Fritzing sketch schema mixeur (saved by Fritzing 0.9.3b)
perfboards: 1

parts:
  Composant1 = Arduino Pro Micro (Clone)  # not connected
  J_Yaw = male pin header, 3 pins [form="♂ (male)"]
  J_Throttle = male pin header, 3 pins [form="♂ (male)"]  # not connected
  J_Motor_Left = male pin header, 3 pins [form="♂ (male)"]  # not connected
  J_Motor_Right = male pin header, 3 pins [form="♂ (male)"]
  J_In3 = male pin header, 3 pins [form="♂ (male)"]  # not connected
  J_In4 = male pin header, 3 pins [form="♂ (male)"]  # not connected

nets:
  N1: J_Yaw.pin1, J_Motor_Right.pin1
